# Fritzing sketch Fritzing_resistances (saved by Fritzing 0.9.4)
breadboards: 1

parts:
  R1 = Resistor [tolerance=±5% resistance=1k package=THT]
  R2 = Resistor [tolerance=±5% resistance=2k package=THT]
  R3 = Resistor [tolerance=±5% resistance=2k package=THT]
  R4 = Resistor [tolerance=±5% resistance=1k package=THT]
  Part1 = Arduino Ethernet Shield (Rev3)

nets:
  N1: R1.Pin_0, Part1.A0, Part1.5V
  N2: R1.Pin_1, R2.Pin_0, R3.Pin_0
  N3: R2.Pin_1, R3.Pin_1, R4.Pin_1, Part1.A1
  N4: R4.Pin_0, Part1.GND
