# Fritzing sketch resistance (saved by Fritzing 0.9.4)
breadboards: 1

parts:
  Part1 = Arduino Uno (Rev3)
  R1 = Resistor [tolerance=±5% resistance=2k package=THT]
  R2 = Resistor [tolerance=±5% resistance=2k package=THT]
  R3 = Resistor [tolerance=±5% resistance=2k package=THT]
  R4 = Resistor [tolerance=±5% resistance=2k package=THT]

nets:
  N1: Part1.A0, Part1.5V, R1.Pin_1, R2.Pin_1, R3.Pin_0
  N2: Part1.A1, R1.Pin_0, R2.Pin_0, R3.Pin_1, R4.Pin_1
  N3: Part1.GND, R4.Pin_0
